# Fritzing sketch Counter (saved by Fritzing 0.9.4)
breadboards: 1

parts:
  R1 = Resistor [tolerance=±5% resistance=220 package="2512 [SMD]"]
  R2 = Resistor [tolerance=±5% resistance=220 package="2512 [SMD]"]
  part = Resistor [tolerance=±5% resistance=220 package="2512 [SMD]"]
  R4 = Resistor [tolerance=±5% resistance=220 package="2512 [SMD]"]
  R5 = Resistor [tolerance=±5% resistance=220 package="2512 [SMD]"]
  R6 = Resistor [tolerance=±5% resistance=220 package="2512 [SMD]"]
  R7 = Resistor [tolerance=±5% resistance=220 package="2512 [SMD]"]
  R8 = Resistor [tolerance=±5% resistance=220 package="2512 [SMD]"]
  Part1 = Arduino Uno (Rev3)
  Pushbutton = Pushbutton [package="[THT]"]
  R9 = Resistor [tolerance=±5% resistance=1k package=THT]
  7_Segment = 7 Segment Display
  C1 = Film/Foil Capacitor [capacitance=100nF voltage=35V package="5mm [THT, pp]"]

nets:
  N1: R1.Pin_0, 7_Segment.Segment_DP
  N2: R1.Pin_1, Part1.D7
  N3: R2.Pin_0, 7_Segment.Segment_C
  N4: R2.Pin_1, Part1.D2
  N5: part.Pin_0, Part1.D3_PWM
  N6: part.Pin_1, 7_Segment.Segment_D
  N7: R4.Pin_0, Part1.D4
  N8: R4.Pin_1, 7_Segment.Segment_E
  N9: R5.Pin_0, Part1.D6_PWM
  N10: R5.Pin_1, 7_Segment.Segment_G
  N11: R6.Pin_0, Part1.D5_PWM
  N12: R6.Pin_1, 7_Segment.Segment_F
  N13: R7.Pin_0, 7_Segment.Segment_A
  N14: R7.Pin_1, Part1.D0/RX
  N15: R8.Pin_0, 7_Segment.Segment_B
  N16: R8.Pin_1, Part1.D1/TX
  N17: Part1.D8, Pushbutton.Pin_3, Pushbutton.Pin_4, R9.Pin_0, C1.-
  N18: Part1.GND, R9.Pin_1, 7_Segment.common_cathode
  N19: Part1.5V, Pushbutton.Pin_1, Pushbutton.Pin_2, C1.+
